// Logisim project Processador.circ as structural Verilog: 2 circuits, main circuit main
module main (
  output [7:0] out_1
);

  wire Clk;
  wire [7:0] adder_1_out, PC_q;

  Register PC (.D(adder_1_out), .en(1'b1), .clk(Clk), .Q(PC_q));  // open: clr
  Clock clock_1 (.out(Clk));
  Adder adder_1 (.a(PC_q), .b(8'h1), .out(adder_1_out));  // open: cin, cout
  ROM rom_1 (.addr(PC_q), .data(out_1));
  BancoDeRegistradores bancoderegistradores_1 ();  // open: rs1, rs2, rd, DADO, W, A, B
endmodule

module BancoDeRegistradores (
  input  [3:0] rs1,
  input  [3:0] rs2,
  input  [3:0] rd,
  input  [19:0] DADO,
  input  W,
  output [19:0] A,
  output [19:0] B
);

  wire CLK, w00, w01, w02, w03, w04, w05, w06, w07, w08, w09, w10, w11, w12, w13, w14, w15;
  wire [19:0] vr00, vr01, vr02, vr03, vr04, vr05, vr06, vr07, vr08, vr09, vr10, vr11, vr12, vr13, vr14, vr15;

  Clock clock_1 (.out(CLK));
  Register #(.width(20)) R00 (.D(DADO), .en(w00), .clk(CLK), .Q(vr00));  // open: clr
  Register #(.width(20)) R01 (.D(DADO), .en(w01), .clk(CLK), .Q(vr01));  // open: clr
  Register #(.width(20)) R02 (.D(DADO), .en(w02), .clk(CLK), .Q(vr02));  // open: clr
  Register #(.width(20)) R03 (.D(DADO), .en(w03), .clk(CLK), .Q(vr03));  // open: clr
  Register #(.width(20)) R04 (.D(DADO), .en(w04), .clk(CLK), .Q(vr04));  // open: clr
  Register #(.width(20)) R05 (.D(DADO), .en(w05), .clk(CLK), .Q(vr05));  // open: clr
  Register #(.width(20)) R06 (.D(DADO), .en(w06), .clk(CLK), .Q(vr06));  // open: clr
  Register #(.width(20)) R07 (.D(DADO), .en(w07), .clk(CLK), .Q(vr07));  // open: clr
  Register #(.width(20)) R08 (.D(DADO), .en(w08), .clk(CLK), .Q(vr08));  // open: clr
  Register #(.width(20)) R09 (.D(DADO), .en(w09), .clk(CLK), .Q(vr09));  // open: clr
  Register #(.width(20)) R10 (.D(DADO), .en(w10), .clk(CLK), .Q(vr10));  // open: clr
  Register #(.width(20)) R11 (.D(DADO), .en(w11), .clk(CLK), .Q(vr11));  // open: clr
  Register #(.width(20)) R12 (.D(DADO), .en(w12), .clk(CLK), .Q(vr12));  // open: clr
  Register #(.width(20)) R13 (.D(DADO), .en(w13), .clk(CLK), .Q(vr13));  // open: clr
  Register #(.width(20)) R14 (.D(DADO), .en(w14), .clk(CLK), .Q(vr14));  // open: clr
  Register #(.width(20)) R15 (.D(DADO), .en(w15), .clk(CLK), .Q(vr15));  // open: clr
  Demultiplexer #(.select(4)) demultiplexer_1 (
    .out0(w00), .out1(w01), .out2(w02), .out3(w03), .out4(w04), .out5(w05), .out6(w06), .out7(w07),
    .out8(w08), .out9(w09), .out10(w10), .out11(w11), .out12(w12), .out13(w13), .out14(w14), .out15(w15),
    .in(W), .sel(rd));
  Multiplexer #(.select(4), .width(20)) multiplexer_1 (
    .in0(vr00), .in1(vr01), .in2(vr02), .in3(vr03), .in4(vr04), .in5(vr05), .in6(vr06), .in7(vr07),
    .in8(vr08), .in9(vr09), .in10(vr10), .in11(vr11), .in12(vr12), .in13(vr13), .in14(vr14), .in15(vr15),
    .out(A), .sel(rs1));
  Multiplexer #(.select(4), .width(20)) multiplexer_2 (
    .in0(vr00), .in1(vr01), .in2(vr02), .in3(vr03), .in4(vr04), .in5(vr05), .in6(vr06), .in7(vr07),
    .in8(vr08), .in9(vr09), .in10(vr10), .in11(vr11), .in12(vr12), .in13(vr13), .in14(vr14), .in15(vr15),
    .out(B), .sel(rs2));

  // Other names for the same wires on the sheet: WD[19:0] = DADO
endmodule
